# Fritzing sketch circuit_01 (saved by Fritzing 0.9.3b)
breadboards: 1

parts:
  Part1 = Arduino Uno (Rev3)
  R1 = Resistor [tolerance=±5% resistance=220 package=THT]
  MOTOR1 = Vibration Motor

nets:
  N1: Part1.GND, MOTOR1.NEG
  N2: Part1.D3_PWM, R1.Pin_0
  N3: R1.Pin_1, MOTOR1.POS

custom parts:
  Vibration Motor: An eccentric vibration motor!
